// Logisim project letras completo - copia.circ as structural Verilog
module Letras (
  input  A,
  input  B,
  input  C,
  input  D,
  output e,
  output c_2,
  output a_2,
  output f,
  output g,
  output d_2,
  output b_2,
  output P
);

  wire and_1_out, and_2_out, and_3_out, and_4_out, and_5_out, and_6_out, and_7_out, and_8_out, and_9_out,
       and_10_out, and_11_out, and_12_out, and_13_out, and_14_out, and_15_out, and_16_out, and_17_out,
       and_18_out, and_19_out, and_20_out, not_1_out, not_2_out, not_3_out, not_4_out, not_5_out, not_6_out,
       not_7_out, not_8_out, not_9_out, not_10_out, not_11_out, not_12_out, not_13_out, not_14_out,
       not_15_out, not_16_out, not_17_out, not_18_out, not_19_out, not_20_out, not_21_out, not_22_out,
       not_23_out, not_24_out, not_25_out, not_26_out, not_27_out, not_28_out, not_29_out, not_30_out,
       not_31_out, not_32_out;

  not not_1 (not_1_out, A);
  and and_1 (and_1_out, not_1_out, not_2_out, not_3_out);
  not not_2 (not_2_out, B);
  not not_3 (not_3_out, D);
  not not_4 (not_4_out, B);
  and and_2 (and_2_out, not_4_out, C);
  not not_5 (not_5_out, A);
  and and_3 (and_3_out, not_5_out, B, not_6_out);
  not not_6 (not_6_out, C);
  and and_4 (and_4_out, B, not_7_out, not_8_out);
  not not_7 (not_7_out, C);
  not not_8 (not_8_out, D);
  not not_9 (not_9_out, B);
  not not_10 (not_10_out, C);
  and and_5 (and_5_out, not_9_out, not_10_out, not_11_out);
  not not_11 (not_11_out, D);
  not not_12 (not_12_out, C);
  and and_6 (and_6_out, B, not_12_out, D);
  and and_7 (and_7_out, B, C, not_13_out);
  not not_13 (not_13_out, D);
  and and_8 (and_8_out, A, C);
  or or_1 (a_2, and_1_out, and_2_out, and_3_out, and_4_out);
  or or_2 (b_2, and_5_out, and_6_out, and_7_out, and_8_out);
  not not_14 (not_14_out, A);
  not not_15 (not_15_out, B);
  not not_16 (not_16_out, C);
  not not_17 (not_17_out, C);
  not not_18 (not_18_out, D);
  not not_19 (not_19_out, D);
  not not_20 (not_20_out, C);
  not not_21 (not_21_out, A);
  not not_22 (not_22_out, B);
  not not_23 (not_23_out, D);
  and and_9 (and_9_out, not_14_out, not_15_out, not_16_out);
  and and_10 (and_10_out, B, not_17_out, D);
  and and_11 (and_11_out, B, C, not_18_out);
  and and_12 (and_12_out, A, not_19_out);
  and and_13 (and_13_out, not_20_out, D);
  and and_14 (and_14_out, not_21_out, not_22_out, C);
  and and_15 (and_15_out, A, not_23_out);
  or or_3 (c_2, and_9_out, and_10_out, and_11_out, and_12_out);
  or or_4 (d_2, and_13_out, and_14_out, and_15_out);
  not not_24 (not_24_out, A);
  not not_25 (not_25_out, D);
  not not_26 (not_26_out, A);
  not not_27 (not_27_out, A);
  not not_28 (not_28_out, C);
  not not_29 (not_29_out, B);
  not not_30 (not_30_out, C);
  not not_31 (not_31_out, D);
  and and_16 (and_16_out, not_24_out, not_25_out);
  not not_32 (not_32_out, B);
  or or_5 (f, not_26_out, D, C, B);
  and and_17 (and_17_out, not_27_out, not_28_out);
  and and_18 (and_18_out, not_29_out, C, D);
  and and_19 (and_19_out, B, not_30_out);
  and and_20 (and_20_out, B, not_31_out);
  or or_6 (e, and_16_out, not_32_out, C);
  or or_7 (g, and_17_out, and_18_out, and_19_out, and_20_out);

  assign P = 1'b0;
endmodule

module LETRA_COM (
  input  A,
  input  B,
  input  C,
  input  D,
  output a_2,
  output b_2,
  output c_2,
  output d_2,
  output e,
  output f,
  output g,
  output P
);
endmodule

module _1 (
  input  A,
  input  B,
  input  C,
  input  D,
  output a_2,
  output b_2,
  output c_2,
  output d_2,
  output e,
  output f,
  output g,
  output P
);

  wire and_1_out, and_2_out, and_3_out, and_4_out, and_5_out, not_1_out, not_2_out, not_3_out, not_4_out,
       not_5_out, not_6_out, not_7_out, not_8_out, not_9_out, not_10_out, not_11_out, not_12_out, not_13_out,
       not_14_out;

  not not_1 (not_1_out, A);
  not not_2 (not_2_out, B);
  not not_3 (not_3_out, C);
  not not_4 (not_4_out, D);
  not not_5 (not_5_out, A);
  not not_6 (not_6_out, B);
  not not_7 (not_7_out, D);
  not not_8 (not_8_out, A);
  not not_9 (not_9_out, B);
  not not_10 (not_10_out, A);
  not not_11 (not_11_out, C);
  not not_12 (not_12_out, D);
  not not_13 (not_13_out, A);
  not not_14 (not_14_out, C);
  and and_1 (and_1_out, not_1_out, not_2_out, not_3_out, not_4_out);
  and and_2 (and_2_out, not_5_out, not_6_out, C, not_7_out);
  and and_3 (and_3_out, not_8_out, not_9_out, C, D);
  and and_4 (and_4_out, not_10_out, B, not_11_out, not_12_out);
  and and_5 (and_5_out, not_13_out, B, not_14_out, D);
  or or_1 (a_2, and_1_out, and_2_out, and_3_out, and_4_out, and_5_out);
endmodule

module AF (
  input  A,
  input  B,
  input  C,
  input  D,
  output a_2
);

  wire and_1_out, and_2_out, and_3_out, and_4_out, and_5_out, and_6_out, and_7_out, and_8_out, and_9_out,
       not_1_out, not_2_out, not_3_out, not_4_out, not_5_out, not_6_out, not_7_out, not_8_out, not_9_out,
       not_10_out, not_11_out, not_12_out, not_13_out, not_14_out, not_15_out, not_16_out, not_17_out,
       not_18_out, not_19_out, not_20_out;

  not not_1 (not_1_out, A);
  not not_2 (not_2_out, B);
  not not_3 (not_3_out, C);
  not not_4 (not_4_out, D);
  not not_5 (not_5_out, A);
  not not_6 (not_6_out, B);
  not not_7 (not_7_out, D);
  not not_8 (not_8_out, A);
  not not_9 (not_9_out, B);
  not not_10 (not_10_out, A);
  not not_11 (not_11_out, C);
  not not_12 (not_12_out, D);
  not not_13 (not_13_out, A);
  not not_14 (not_14_out, C);
  not not_15 (not_15_out, B);
  not not_16 (not_16_out, D);
  not not_17 (not_17_out, B);
  not not_18 (not_18_out, C);
  not not_19 (not_19_out, D);
  not not_20 (not_20_out, C);
  and and_1 (and_1_out, not_1_out, not_2_out, not_3_out, not_4_out);
  and and_2 (and_2_out, not_5_out, not_6_out, C, not_7_out);
  and and_3 (and_3_out, not_8_out, not_9_out, C, D);
  and and_4 (and_4_out, not_10_out, B, not_11_out, not_12_out);
  and and_5 (and_5_out, not_13_out, B, not_14_out, D);
  and and_6 (and_6_out, A, not_15_out, C, not_16_out);
  and and_7 (and_7_out, A, not_17_out, C, D);
  and and_8 (and_8_out, A, B, not_18_out, not_19_out);
  and and_9 (and_9_out, A, B, not_20_out, D);
  or or_1 (a_2, and_1_out, and_2_out, and_3_out, and_4_out, and_5_out, and_6_out, and_7_out, and_8_out, and_9_out);
endmodule

module Circuito_completo (
  input  A,
  input  B,
  input  C,
  input  D,
  output a_2,
  output b_2,
  output c_2,
  output d_2,
  output e,
  output f,
  output g,
  output P
);

  wire and_1_out, and_2_out, and_3_out, and_4_out, and_5_out, and_6_out, and_7_out, and_8_out, and_9_out,
       and_10_out, and_11_out, and_12_out, and_13_out, and_14_out, and_15_out, and_16_out, and_17_out,
       and_18_out, and_19_out, and_20_out, and_21_out, and_22_out, and_23_out, and_24_out, and_25_out,
       and_26_out, and_27_out, and_28_out, and_29_out, and_30_out, and_31_out, and_32_out, and_33_out,
       and_34_out, and_35_out, and_36_out, and_37_out, and_38_out, and_39_out, and_40_out, and_41_out,
       and_42_out, and_43_out, and_44_out, and_45_out, and_46_out, and_47_out, and_48_out, and_49_out,
       and_50_out, and_51_out, and_52_out, and_53_out, and_54_out, and_55_out, and_56_out, and_57_out,
       and_58_out, and_59_out, and_60_out, and_61_out, and_62_out, and_63_out, and_64_out, and_65_out,
       and_66_out, and_67_out, and_68_out, and_69_out, and_70_out, and_71_out, and_72_out, and_73_out,
       and_74_out, and_75_out, and_76_out, and_77_out, and_78_out, and_79_out, and_80_out, and_81_out,
       and_82_out, and_83_out, and_84_out, and_85_out, and_86_out, and_87_out, and_88_out, and_89_out,
       and_90_out, and_91_out, and_92_out, and_93_out, and_94_out, and_95_out, and_96_out, and_97_out,
       and_98_out, and_99_out, and_100_out, and_101_out, and_102_out, and_103_out, and_104_out, and_105_out,
       and_106_out, and_107_out, and_108_out, and_109_out, and_110_out, and_111_out, and_112_out,
       and_113_out, and_114_out, and_115_out, and_116_out, and_117_out, and_118_out, and_119_out,
       and_120_out, and_121_out, and_122_out, and_123_out, and_124_out, and_125_out, and_126_out,
       and_127_out, and_128_out, and_129_out, and_130_out, and_131_out, and_132_out, and_133_out,
       and_134_out, and_135_out, and_136_out, and_137_out, and_138_out, and_139_out, and_140_out,
       and_141_out, and_142_out, and_143_out, and_144_out, and_145_out, and_146_out, and_147_out,
       and_148_out, and_149_out, and_150_out, and_151_out, and_152_out, and_153_out, and_154_out,
       and_155_out, and_156_out, and_157_out, and_158_out, and_159_out, and_160_out, and_161_out,
       and_162_out, and_163_out, and_164_out, and_165_out, and_166_out, and_167_out, and_168_out,
       and_169_out, and_170_out, and_171_out, and_172_out, and_173_out, and_174_out, and_175_out,
       and_176_out, and_177_out, and_178_out, and_179_out, and_180_out, and_181_out, and_182_out,
       and_183_out, and_184_out, and_185_out, and_186_out, and_187_out, and_188_out, and_189_out,
       and_190_out, and_191_out, and_192_out, and_193_out, and_194_out, and_195_out, and_196_out,
       and_197_out, and_198_out, not_1_out, not_2_out, not_3_out, not_4_out, not_5_out, not_6_out, not_7_out,
       not_8_out, not_9_out, not_10_out, not_11_out, not_12_out, not_13_out, not_14_out, not_15_out,
       not_16_out, not_17_out, not_18_out, not_19_out, not_20_out, not_21_out, not_22_out, not_23_out,
       not_24_out, not_25_out, not_26_out, not_27_out, not_28_out, not_29_out, not_30_out, not_31_out,
       not_32_out, not_33_out, not_34_out, not_35_out, not_36_out, not_37_out, not_38_out, not_39_out,
       not_40_out, not_41_out, not_42_out, not_43_out, not_44_out, not_45_out, not_46_out, not_47_out,
       not_48_out, not_49_out, not_50_out, not_51_out, not_52_out, not_53_out, not_54_out, not_55_out,
       not_56_out, not_57_out, not_58_out, not_59_out, not_60_out, not_61_out, not_62_out, not_63_out,
       not_64_out, not_65_out, not_66_out, not_67_out, not_68_out, not_69_out, not_70_out, not_71_out,
       not_72_out, not_73_out, not_74_out, not_75_out, not_76_out, not_77_out, not_78_out, not_79_out,
       not_80_out, not_81_out, not_82_out, not_83_out, not_84_out, not_85_out, not_86_out, not_87_out,
       not_88_out, not_89_out, not_90_out, not_91_out, not_92_out, not_93_out, not_94_out, not_95_out,
       not_96_out, not_97_out, not_98_out, not_99_out, not_100_out, not_101_out, not_102_out, not_103_out,
       not_104_out, not_105_out, not_106_out, not_107_out, not_108_out, not_109_out, not_110_out,
       not_111_out, not_112_out, not_113_out, not_114_out, not_115_out, not_116_out, not_117_out,
       not_118_out, not_119_out, not_120_out, not_121_out, not_122_out, not_123_out, not_124_out,
       not_125_out, not_126_out, not_127_out, not_128_out, not_129_out, not_130_out, not_131_out,
       not_132_out, not_133_out, not_134_out, not_135_out, not_136_out, not_137_out, not_138_out,
       not_139_out, not_140_out, not_141_out, not_142_out, not_143_out, not_144_out, not_145_out,
       not_146_out, not_147_out, not_148_out, or_1_out, or_2_out, or_3_out, or_4_out, or_5_out, or_6_out,
       or_7_out, or_8_out, or_9_out, or_10_out, or_11_out, or_12_out, or_13_out, or_14_out, or_15_out,
       or_16_out, or_17_out, or_18_out, or_19_out, or_20_out, or_21_out, or_22_out, or_23_out, or_24_out,
       or_25_out, or_26_out, or_27_out, or_28_out, or_29_out, or_30_out, or_31_out, or_32_out, or_33_out,
       or_34_out, or_35_out, or_36_out, or_37_out, or_38_out, or_39_out, or_40_out, or_41_out, or_42_out,
       or_43_out, or_44_out, or_47_out, or_48_out, or_49_out, or_50_out, or_51_out, or_52_out, or_53_out,
       or_54_out;

  not not_1 (not_1_out, A);
  and and_1 (and_1_out, not_1_out, not_2_out);
  not not_2 (not_2_out, B);
  not not_3 (not_3_out, C);
  and and_2 (and_2_out, not_3_out, not_4_out);
  not not_4 (not_4_out, D);
  not not_5 (not_5_out, A);
  and and_3 (and_3_out, not_5_out, not_6_out);
  not not_6 (not_6_out, B);
  and and_4 (and_4_out, C, not_7_out);
  not not_7 (not_7_out, D);
  not not_8 (not_8_out, A);
  not not_9 (not_9_out, B);
  not not_10 (not_10_out, A);
  not not_11 (not_11_out, C);
  not not_12 (not_12_out, D);
  not not_13 (not_13_out, A);
  not not_14 (not_14_out, C);
  not not_15 (not_15_out, B);
  not not_16 (not_16_out, D);
  not not_17 (not_17_out, B);
  not not_18 (not_18_out, C);
  not not_19 (not_19_out, D);
  not not_20 (not_20_out, C);
  not not_21 (not_21_out, A);
  and and_5 (and_5_out, not_21_out, not_22_out);
  not not_22 (not_22_out, B);
  not not_23 (not_23_out, C);
  and and_6 (and_6_out, not_23_out, not_24_out);
  not not_24 (not_24_out, D);
  not not_25 (not_25_out, A);
  and and_7 (and_7_out, not_25_out, B);
  not not_26 (not_26_out, C);
  and and_8 (and_8_out, not_26_out, D);
  not not_27 (not_27_out, A);
  and and_9 (and_9_out, not_27_out, B);
  and and_10 (and_10_out, C, not_28_out);
  not not_28 (not_28_out, D);
  and and_11 (and_11_out, A, not_29_out);
  not not_29 (not_29_out, B);
  not not_30 (not_30_out, C);
  and and_12 (and_12_out, not_30_out, not_31_out);
  not not_31 (not_31_out, D);
  and and_13 (and_13_out, A, not_32_out);
  not not_32 (not_32_out, B);
  and and_14 (and_14_out, C, not_33_out);
  not not_33 (not_33_out, D);
  and and_15 (and_15_out, A, not_34_out);
  not not_34 (not_34_out, B);
  and and_16 (and_16_out, C, D);
  not not_35 (not_35_out, C);
  not not_36 (not_36_out, A);
  and and_17 (and_17_out, not_36_out, not_37_out);
  not not_37 (not_37_out, B);
  not not_38 (not_38_out, C);
  and and_18 (and_18_out, not_38_out, not_39_out);
  not not_39 (not_39_out, D);
  not not_40 (not_40_out, A);
  and and_19 (and_19_out, not_40_out, not_41_out);
  not not_41 (not_41_out, B);
  not not_42 (not_42_out, C);
  and and_20 (and_20_out, not_42_out, D);
  not not_43 (not_43_out, A);
  and and_21 (and_21_out, not_43_out, B);
  not not_44 (not_44_out, C);
  and and_22 (and_22_out, not_44_out, D);
  not not_45 (not_45_out, A);
  and and_23 (and_23_out, not_45_out, B);
  and and_24 (and_24_out, C, not_46_out);
  not not_46 (not_46_out, D);
  and and_25 (and_25_out, A, not_47_out);
  not not_47 (not_47_out, B);
  not not_48 (not_48_out, C);
  and and_26 (and_26_out, not_48_out, not_49_out);
  not not_49 (not_49_out, D);
  and and_27 (and_27_out, A, not_50_out);
  not not_50 (not_50_out, B);
  and and_28 (and_28_out, C, not_51_out);
  not not_51 (not_51_out, D);
  and and_29 (and_29_out, A, not_52_out);
  not not_52 (not_52_out, B);
  and and_30 (and_30_out, C, D);
  and and_31 (and_31_out, A, B);
  not not_53 (not_53_out, C);
  and and_32 (and_32_out, not_53_out, D);
  not not_54 (not_54_out, A);
  and and_33 (and_33_out, not_54_out, not_55_out);
  not not_55 (not_55_out, B);
  not not_56 (not_56_out, C);
  and and_34 (and_34_out, not_56_out, D);
  not not_57 (not_57_out, A);
  and and_35 (and_35_out, not_57_out, not_58_out);
  not not_58 (not_58_out, B);
  and and_36 (and_36_out, C, not_59_out);
  not not_59 (not_59_out, D);
  not not_60 (not_60_out, A);
  not not_61 (not_61_out, B);
  not not_62 (not_62_out, A);
  not not_63 (not_63_out, C);
  not not_64 (not_64_out, B);
  not not_65 (not_65_out, C);
  not not_66 (not_66_out, D);
  not not_67 (not_67_out, B);
  not not_68 (not_68_out, C);
  not not_69 (not_69_out, B);
  not not_70 (not_70_out, D);
  not not_71 (not_71_out, C);
  not not_72 (not_72_out, D);
  not not_73 (not_73_out, C);
  not not_74 (not_74_out, A);
  and and_37 (and_37_out, not_74_out, not_75_out);
  not not_75 (not_75_out, B);
  not not_76 (not_76_out, C);
  and and_38 (and_38_out, not_76_out, not_77_out);
  not not_77 (not_77_out, D);
  not not_78 (not_78_out, A);
  and and_39 (and_39_out, not_78_out, not_79_out);
  not not_79 (not_79_out, B);
  not not_80 (not_80_out, C);
  and and_40 (and_40_out, not_80_out, D);
  not not_81 (not_81_out, A);
  not not_82 (not_82_out, B);
  not not_83 (not_83_out, D);
  not not_84 (not_84_out, A);
  and and_41 (and_41_out, not_84_out, not_85_out);
  not not_85 (not_85_out, B);
  and and_42 (and_42_out, C, D);
  not not_86 (not_86_out, A);
  and and_43 (and_43_out, not_86_out, B);
  not not_87 (not_87_out, C);
  and and_44 (and_44_out, not_87_out, not_88_out);
  not not_88 (not_88_out, D);
  not not_89 (not_89_out, A);
  and and_45 (and_45_out, A, not_90_out);
  not not_90 (not_90_out, B);
  not not_91 (not_91_out, C);
  and and_46 (and_46_out, not_91_out, not_92_out);
  not not_92 (not_92_out, D);
  and and_47 (and_47_out, A, not_93_out);
  not not_93 (not_93_out, B);
  not not_94 (not_94_out, C);
  and and_48 (and_48_out, not_94_out, not_95_out);
  not not_95 (not_95_out, D);
  not not_96 (not_96_out, B);
  not not_97 (not_97_out, C);
  not not_98 (not_98_out, B);
  not not_99 (not_99_out, D);
  not not_100 (not_100_out, B);
  not not_101 (not_101_out, A);
  and and_49 (and_49_out, not_101_out, not_102_out);
  not not_102 (not_102_out, B);
  not not_103 (not_103_out, C);
  and and_50 (and_50_out, not_103_out, not_104_out);
  not not_104 (not_104_out, D);
  not not_105 (not_105_out, A);
  and and_51 (and_51_out, not_105_out, not_106_out);
  not not_106 (not_106_out, B);
  not not_107 (not_107_out, C);
  and and_52 (and_52_out, not_107_out, D);
  not not_108 (not_108_out, A);
  and and_53 (and_53_out, not_108_out, not_109_out);
  not not_109 (not_109_out, B);
  and and_54 (and_54_out, C, not_110_out);
  not not_110 (not_110_out, D);
  not not_111 (not_111_out, A);
  and and_55 (and_55_out, not_111_out, not_112_out);
  not not_112 (not_112_out, B);
  and and_56 (and_56_out, C, D);
  not not_113 (not_113_out, A);
  and and_57 (and_57_out, not_113_out, B);
  not not_114 (not_114_out, C);
  and and_58 (and_58_out, not_114_out, not_115_out);
  not not_115 (not_115_out, D);
  not not_116 (not_116_out, A);
  and and_59 (and_59_out, not_116_out, B);
  not not_117 (not_117_out, C);
  and and_60 (and_60_out, not_117_out, D);
  not not_118 (not_118_out, A);
  not not_119 (not_119_out, D);
  not not_120 (not_120_out, A);
  and and_61 (and_61_out, not_120_out, B);
  and and_62 (and_62_out, C, D);
  and and_63 (and_63_out, A, not_121_out);
  not not_121 (not_121_out, B);
  not not_122 (not_122_out, C);
  and and_64 (and_64_out, not_122_out, D);
  not not_123 (not_123_out, B);
  not not_124 (not_124_out, D);
  and and_65 (and_65_out, A, not_125_out);
  not not_125 (not_125_out, B);
  and and_66 (and_66_out, C, D);
  and and_67 (and_67_out, A, B);
  not not_126 (not_126_out, C);
  and and_68 (and_68_out, not_126_out, not_127_out);
  not not_127 (not_127_out, D);
  not not_128 (not_128_out, C);
  not not_129 (not_129_out, A);
  and and_69 (and_69_out, not_129_out, not_130_out);
  not not_130 (not_130_out, B);
  not not_131 (not_131_out, C);
  and and_70 (and_70_out, not_131_out, not_132_out);
  not not_132 (not_132_out, D);
  not not_133 (not_133_out, A);
  and and_71 (and_71_out, not_133_out, not_134_out);
  not not_134 (not_134_out, B);
  not not_135 (not_135_out, C);
  and and_72 (and_72_out, not_135_out, D);
  not not_136 (not_136_out, A);
  not not_137 (not_137_out, B);
  not not_138 (not_138_out, A);
  not not_139 (not_139_out, C);
  not not_140 (not_140_out, D);
  not not_141 (not_141_out, A);
  not not_142 (not_142_out, C);
  not not_143 (not_143_out, A);
  not not_144 (not_144_out, D);
  not not_145 (not_145_out, B);
  not not_146 (not_146_out, C);
  not not_147 (not_147_out, D);
  not not_148 (not_148_out, C);
  and and_73 (and_73_out, and_1_out, and_2_out);
  and and_74 (and_74_out, and_3_out, and_4_out);
  and and_75 (and_75_out, not_8_out, not_9_out);
  and and_76 (and_76_out, C, D);
  and and_77 (and_77_out, not_10_out, B);
  and and_78 (and_78_out, not_11_out, not_12_out);
  and and_79 (and_79_out, not_13_out, B);
  and and_80 (and_80_out, not_14_out, D);
  and and_81 (and_81_out, A, not_15_out);
  and and_82 (and_82_out, C, not_16_out);
  and and_83 (and_83_out, A, not_17_out);
  and and_84 (and_84_out, C, D);
  and and_85 (and_85_out, A, B);
  and and_86 (and_86_out, not_18_out, not_19_out);
  and and_87 (and_87_out, A, B);
  and and_88 (and_88_out, not_20_out, D);
  and and_89 (and_89_out, and_5_out, and_6_out);
  and and_90 (and_90_out, and_7_out, and_8_out);
  and and_91 (and_91_out, and_9_out, and_10_out);
  and and_92 (and_92_out, and_11_out, and_12_out);
  and and_93 (and_93_out, and_13_out, and_14_out);
  and and_94 (and_94_out, and_15_out, and_16_out);
  and and_95 (and_95_out, A, B);
  and and_96 (and_96_out, not_35_out, D);
  and and_97 (and_97_out, and_17_out, and_18_out);
  and and_98 (and_98_out, and_19_out, and_20_out);
  and and_99 (and_99_out, and_21_out, and_22_out);
  and and_100 (and_100_out, and_23_out, and_24_out);
  and and_101 (and_101_out, and_25_out, and_26_out);
  and and_102 (and_102_out, and_27_out, and_28_out);
  and and_103 (and_103_out, and_29_out, and_30_out);
  and and_104 (and_104_out, and_31_out, and_32_out);
  and and_105 (and_105_out, and_33_out, and_34_out);
  and and_106 (and_106_out, and_35_out, and_36_out);
  and and_107 (and_107_out, not_60_out, not_61_out);
  and and_108 (and_108_out, C, D);
  and and_109 (and_109_out, not_62_out, B);
  and and_110 (and_110_out, not_63_out, D);
  and and_111 (and_111_out, A, not_64_out);
  and and_112 (and_112_out, not_65_out, not_66_out);
  and and_113 (and_113_out, A, not_67_out);
  and and_114 (and_114_out, not_68_out, D);
  and and_115 (and_115_out, A, not_69_out);
  and and_116 (and_116_out, C, not_70_out);
  and and_117 (and_117_out, A, B);
  and and_118 (and_118_out, not_71_out, not_72_out);
  and and_119 (and_119_out, A, B);
  and and_120 (and_120_out, not_73_out, D);
  and and_121 (and_121_out, and_37_out, and_38_out);
  and and_122 (and_122_out, and_39_out, and_40_out);
  and and_123 (and_123_out, not_81_out, not_82_out);
  and and_124 (and_124_out, C, not_83_out);
  and and_125 (and_125_out, and_41_out, and_42_out);
  and and_126 (and_126_out, and_43_out, and_44_out);
  and and_127 (and_127_out, not_89_out, B);
  and and_128 (and_128_out, C, D);
  and and_129 (and_129_out, and_45_out, and_46_out);
  and and_130 (and_130_out, and_47_out, and_48_out);
  and and_131 (and_131_out, A, not_96_out);
  and and_132 (and_132_out, not_97_out, D);
  and and_133 (and_133_out, A, not_98_out);
  and and_134 (and_134_out, C, not_99_out);
  and and_135 (and_135_out, A, not_100_out);
  and and_136 (and_136_out, C, D);
  and and_137 (and_137_out, and_49_out, and_50_out);
  and and_138 (and_138_out, and_51_out, and_52_out);
  and and_139 (and_139_out, and_53_out, and_54_out);
  and and_140 (and_140_out, and_55_out, and_56_out);
  and and_141 (and_141_out, and_57_out, and_58_out);
  and and_142 (and_142_out, and_59_out, and_60_out);
  and and_143 (and_143_out, not_118_out, B);
  and and_144 (and_144_out, C, not_119_out);
  and and_145 (and_145_out, and_61_out, and_62_out);
  and and_146 (and_146_out, and_63_out, and_64_out);
  and and_147 (and_147_out, A, not_123_out);
  and and_148 (and_148_out, C, not_124_out);
  and and_149 (and_149_out, and_65_out, and_66_out);
  and and_150 (and_150_out, and_67_out, and_68_out);
  and and_151 (and_151_out, A, B);
  and and_152 (and_152_out, not_128_out, D);
  and and_153 (and_153_out, and_69_out, and_70_out);
  and and_154 (and_154_out, and_71_out, and_72_out);
  and and_155 (and_155_out, not_136_out, not_137_out);
  and and_156 (and_156_out, C, D);
  and and_157 (and_157_out, not_138_out, B);
  and and_158 (and_158_out, not_139_out, not_140_out);
  and and_159 (and_159_out, not_141_out, B);
  and and_160 (and_160_out, not_142_out, D);
  and and_161 (and_161_out, not_143_out, B);
  and and_162 (and_162_out, C, not_144_out);
  and and_163 (and_163_out, A, not_145_out);
  and and_164 (and_164_out, C, D);
  and and_165 (and_165_out, A, B);
  and and_166 (and_166_out, not_146_out, not_147_out);
  and and_167 (and_167_out, A, B);
  and and_168 (and_168_out, not_148_out, D);
  or or_1 (or_1_out, and_73_out, and_74_out);
  and and_169 (and_169_out, and_75_out, and_76_out);
  and and_170 (and_170_out, and_77_out, and_78_out);
  and and_171 (and_171_out, and_79_out, and_80_out);
  and and_172 (and_172_out, and_81_out, and_82_out);
  and and_173 (and_173_out, and_83_out, and_84_out);
  and and_174 (and_174_out, and_85_out, and_86_out);
  and and_175 (and_175_out, and_87_out, and_88_out);
  or or_2 (or_2_out, and_89_out, and_90_out);
  or or_3 (or_3_out, and_91_out, and_92_out);
  or or_4 (or_4_out, and_93_out, and_94_out);
  and and_176 (and_176_out, and_95_out, and_96_out);
  or or_5 (or_5_out, and_97_out, and_98_out);
  or or_6 (or_6_out, and_99_out, and_100_out);
  or or_7 (or_7_out, and_101_out, and_102_out);
  or or_8 (or_8_out, and_103_out, and_104_out);
  or or_9 (or_9_out, and_105_out, and_106_out);
  and and_177 (and_177_out, and_107_out, and_108_out);
  and and_178 (and_178_out, and_109_out, and_110_out);
  and and_179 (and_179_out, and_111_out, and_112_out);
  and and_180 (and_180_out, and_113_out, and_114_out);
  and and_181 (and_181_out, and_115_out, and_116_out);
  and and_182 (and_182_out, and_117_out, and_118_out);
  and and_183 (and_183_out, and_119_out, and_120_out);
  or or_10 (or_10_out, and_121_out, and_122_out);
  and and_184 (and_184_out, and_123_out, and_124_out);
  or or_11 (or_11_out, and_125_out, and_126_out);
  and and_185 (and_185_out, and_127_out, and_128_out);
  or or_12 (or_12_out, and_129_out, and_130_out);
  and and_186 (and_186_out, and_131_out, and_132_out);
  and and_187 (and_187_out, and_133_out, and_134_out);
  and and_188 (and_188_out, and_135_out, and_136_out);
  or or_13 (or_13_out, and_137_out, and_138_out);
  or or_14 (or_14_out, and_139_out, and_140_out);
  or or_15 (or_15_out, and_141_out, and_142_out);
  and and_189 (and_189_out, and_143_out, and_144_out);
  or or_16 (or_16_out, and_145_out, and_146_out);
  and and_190 (and_190_out, and_147_out, and_148_out);
  or or_17 (or_17_out, and_149_out, and_150_out);
  and and_191 (and_191_out, and_151_out, and_152_out);
  or or_18 (or_18_out, and_153_out, and_154_out);
  and and_192 (and_192_out, and_155_out, and_156_out);
  and and_193 (and_193_out, and_157_out, and_158_out);
  and and_194 (and_194_out, and_159_out, and_160_out);
  and and_195 (and_195_out, and_161_out, and_162_out);
  and and_196 (and_196_out, and_163_out, and_164_out);
  and and_197 (and_197_out, and_165_out, and_166_out);
  and and_198 (and_198_out, and_167_out, and_168_out);
  or or_19 (or_19_out, or_1_out, and_169_out);
  or or_20 (or_20_out, and_170_out, and_171_out);
  or or_21 (or_21_out, and_172_out, and_173_out);
  or or_22 (or_22_out, and_174_out, and_175_out);
  or or_23 (or_23_out, or_2_out, or_3_out);
  or or_24 (or_24_out, or_4_out, and_176_out);
  or or_25 (or_25_out, or_5_out, or_6_out);
  or or_26 (or_26_out, or_7_out, or_8_out);
  or or_27 (or_27_out, or_9_out, and_177_out);
  or or_28 (or_28_out, and_178_out, and_179_out);
  or or_29 (or_29_out, and_180_out, and_181_out);
  or or_30 (or_30_out, and_182_out, and_183_out);
  or or_31 (or_31_out, or_10_out, and_184_out);
  or or_32 (or_32_out, or_11_out, and_185_out);
  or or_33 (or_33_out, or_12_out, and_186_out);
  or or_34 (or_34_out, and_187_out, and_188_out);
  or or_35 (or_35_out, or_13_out, or_14_out);
  or or_36 (or_36_out, or_15_out, and_189_out);
  or or_37 (or_37_out, or_16_out, and_190_out);
  or or_38 (or_38_out, or_17_out, and_191_out);
  or or_39 (or_39_out, or_18_out, and_192_out);
  or or_40 (or_40_out, and_193_out, and_194_out);
  or or_41 (or_41_out, and_195_out, and_196_out);
  or or_42 (or_42_out, and_197_out, and_198_out);
  or or_43 (or_43_out, or_19_out, or_20_out);
  or or_44 (or_44_out, or_21_out, or_22_out);
  or or_45 (b_2, or_23_out, or_24_out);
  or or_46 (c_2, or_25_out, or_26_out);
  or or_47 (or_47_out, or_27_out, or_28_out);
  or or_48 (or_48_out, or_29_out, or_30_out);
  or or_49 (or_49_out, or_31_out, or_32_out);
  or or_50 (or_50_out, or_33_out, or_34_out);
  or or_51 (or_51_out, or_35_out, or_36_out);
  or or_52 (or_52_out, or_37_out, or_38_out);
  or or_53 (or_53_out, or_39_out, or_40_out);
  or or_54 (or_54_out, or_41_out, or_42_out);
  or or_55 (a_2, or_43_out, or_44_out);
  or or_56 (d_2, or_47_out, or_48_out);
  or or_57 (e, or_49_out, or_50_out);
  or or_58 (f, or_51_out, or_52_out);
  or or_59 (g, or_53_out, or_54_out);

  assign P = 1'b0;
endmodule

module Letras_completo (
  input  A,
  input  B,
  input  C,
  input  D,
  output a_2,
  output b_2,
  output c_2,
  output d_2,
  output e,
  output f,
  output g,
  output P
);

  wire and_1_out, and_2_out, and_3_out, and_4_out, and_5_out, and_6_out, and_7_out, and_8_out, and_9_out,
       and_10_out, and_11_out, and_12_out, and_13_out, and_14_out, and_15_out, and_16_out, and_17_out,
       and_18_out, and_19_out, and_20_out, and_21_out, and_22_out, and_23_out, and_24_out, and_25_out,
       and_26_out, and_27_out, and_28_out, and_29_out, and_30_out, and_31_out, and_32_out, and_33_out,
       and_34_out, and_35_out, and_36_out, and_37_out, and_38_out, and_39_out, and_40_out, and_41_out,
       and_42_out, and_43_out, and_44_out, and_45_out, and_46_out, and_47_out, and_48_out, and_49_out,
       and_50_out, and_51_out, and_52_out, and_53_out, and_54_out, and_55_out, and_56_out, and_57_out,
       and_58_out, and_59_out, and_60_out, and_61_out, and_62_out, and_63_out, and_64_out, and_65_out,
       and_66_out, and_67_out, and_68_out, and_69_out, and_70_out, and_71_out, and_72_out, and_73_out,
       and_74_out, and_75_out, and_76_out, and_77_out, and_78_out, and_79_out, and_80_out, and_81_out,
       and_82_out, and_83_out, and_84_out, and_85_out, and_86_out, and_87_out, and_88_out, and_89_out,
       and_90_out, and_91_out, and_92_out, and_93_out, and_94_out, and_95_out, and_96_out, and_97_out,
       and_98_out, and_99_out, and_100_out, and_101_out, and_102_out, and_103_out, and_104_out, and_105_out,
       and_106_out, and_107_out, and_108_out, and_109_out, and_110_out, and_111_out, and_112_out,
       and_113_out, and_114_out, and_115_out, and_116_out, and_117_out, and_118_out, and_119_out,
       and_120_out, and_121_out, and_122_out, and_123_out, and_124_out, and_125_out, and_126_out,
       and_127_out, and_128_out, and_129_out, and_130_out, and_131_out, and_132_out, and_133_out,
       and_134_out, and_135_out, and_136_out, and_137_out, and_138_out, and_139_out, and_140_out,
       and_141_out, and_142_out, and_143_out, and_144_out, and_145_out, and_146_out, and_147_out,
       and_148_out, and_149_out, and_150_out, and_151_out, and_152_out, and_153_out, and_154_out,
       and_155_out, and_156_out, and_157_out, and_158_out, and_159_out, and_160_out, and_161_out,
       and_162_out, and_163_out, and_164_out, and_165_out, and_166_out, and_167_out, and_168_out,
       and_169_out, and_170_out, and_171_out, and_172_out, and_173_out, and_174_out, and_175_out,
       and_176_out, and_177_out, and_178_out, and_179_out, and_180_out, and_181_out, and_182_out,
       and_183_out, and_184_out, and_185_out, and_186_out, and_187_out, and_188_out, and_189_out,
       and_190_out, and_191_out, and_192_out, and_193_out, and_194_out, and_195_out, and_196_out,
       and_197_out, and_198_out, and_199_out, and_200_out, and_201_out, not_1_out, not_2_out, not_3_out,
       not_4_out, not_5_out, not_6_out, not_7_out, not_8_out, not_9_out, not_10_out, not_11_out, not_12_out,
       not_13_out, not_14_out, not_15_out, not_16_out, not_17_out, not_18_out, not_19_out, not_20_out,
       not_21_out, not_22_out, not_23_out, not_24_out, not_25_out, not_26_out, not_27_out, not_28_out,
       not_29_out, not_30_out, not_31_out, not_32_out, not_33_out, not_34_out, not_35_out, not_36_out,
       not_37_out, not_38_out, not_39_out, not_40_out, not_41_out, not_42_out, not_43_out, not_44_out,
       not_45_out, not_46_out, not_47_out, not_48_out, not_49_out, not_50_out, not_51_out, not_52_out,
       not_53_out, not_54_out, not_55_out, not_56_out, not_57_out, not_58_out, not_59_out, not_60_out,
       not_61_out, not_62_out, not_63_out, not_64_out, not_65_out, not_66_out, not_67_out, not_68_out,
       not_69_out, not_70_out, not_71_out, not_72_out, not_73_out, not_74_out, not_75_out, not_76_out,
       not_77_out, not_78_out, not_79_out, not_80_out, not_81_out, not_82_out, not_83_out, not_84_out,
       not_85_out, not_86_out, not_87_out, not_88_out, not_89_out, not_90_out, not_91_out, not_92_out,
       not_93_out, not_94_out, not_95_out, not_96_out, not_97_out, not_98_out, not_99_out, not_100_out,
       not_101_out, not_102_out, not_103_out, not_104_out, not_105_out, not_106_out, not_107_out,
       not_108_out, not_109_out, not_110_out, not_111_out, not_112_out, not_113_out, not_114_out,
       not_115_out, not_116_out, not_117_out, not_118_out, not_119_out, not_120_out, not_121_out,
       not_122_out, not_123_out, not_124_out, not_125_out, not_126_out, not_127_out, not_128_out,
       not_129_out, not_130_out, not_131_out, not_132_out, not_133_out, not_134_out, not_135_out,
       not_136_out, not_137_out, not_138_out, not_139_out, not_140_out, not_141_out, not_142_out,
       not_143_out, not_144_out, not_145_out, not_146_out, not_147_out, not_148_out, not_149_out,
       not_150_out, not_151_out, or_1_out, or_2_out, or_3_out, or_4_out, or_5_out, or_6_out, or_7_out,
       or_8_out, or_9_out, or_10_out, or_11_out, or_12_out, or_13_out, or_14_out, or_15_out, or_16_out,
       or_17_out, or_18_out, or_19_out, or_20_out, or_21_out, or_22_out, or_23_out, or_24_out, or_25_out,
       or_26_out, or_27_out, or_28_out, or_29_out, or_30_out, or_31_out, or_32_out, or_33_out, or_34_out,
       or_35_out, or_36_out, or_37_out, or_38_out, or_39_out, or_40_out, or_41_out, or_42_out, or_43_out,
       or_46_out, or_47_out, or_48_out, or_49_out, or_50_out, or_51_out, or_52_out, or_53_out, or_54_out,
       or_55_out;

  not not_1 (not_1_out, A);
  and and_1 (and_1_out, not_1_out, not_2_out);
  not not_2 (not_2_out, B);
  not not_3 (not_3_out, C);
  and and_2 (and_2_out, not_3_out, not_4_out);
  not not_4 (not_4_out, D);
  not not_5 (not_5_out, A);
  and and_3 (and_3_out, not_5_out, not_6_out);
  not not_6 (not_6_out, B);
  and and_4 (and_4_out, C, not_7_out);
  not not_7 (not_7_out, D);
  not not_8 (not_8_out, A);
  and and_5 (and_5_out, not_8_out, not_9_out);
  not not_9 (not_9_out, B);
  and and_6 (and_6_out, C, D);
  not not_10 (not_10_out, A);
  and and_7 (and_7_out, not_10_out, B);
  not not_11 (not_11_out, C);
  and and_8 (and_8_out, not_11_out, not_12_out);
  not not_12 (not_12_out, D);
  not not_13 (not_13_out, A);
  and and_9 (and_9_out, not_13_out, B);
  not not_14 (not_14_out, C);
  and and_10 (and_10_out, not_14_out, D);
  and and_11 (and_11_out, A, not_15_out);
  not not_15 (not_15_out, B);
  and and_12 (and_12_out, C, not_16_out);
  not not_16 (not_16_out, D);
  and and_13 (and_13_out, A, not_17_out);
  not not_17 (not_17_out, B);
  and and_14 (and_14_out, C, D);
  and and_15 (and_15_out, A, B);
  not not_18 (not_18_out, C);
  and and_16 (and_16_out, not_18_out, not_19_out);
  not not_19 (not_19_out, D);
  not not_20 (not_20_out, A);
  and and_17 (and_17_out, not_20_out, not_21_out);
  not not_21 (not_21_out, B);
  not not_22 (not_22_out, C);
  and and_18 (and_18_out, not_22_out, not_23_out);
  not not_23 (not_23_out, D);
  not not_24 (not_24_out, A);
  and and_19 (and_19_out, not_24_out, B);
  not not_25 (not_25_out, C);
  and and_20 (and_20_out, not_25_out, D);
  not not_26 (not_26_out, A);
  and and_21 (and_21_out, not_26_out, B);
  and and_22 (and_22_out, C, not_27_out);
  not not_27 (not_27_out, D);
  and and_23 (and_23_out, A, not_28_out);
  not not_28 (not_28_out, B);
  not not_29 (not_29_out, C);
  and and_24 (and_24_out, not_29_out, not_30_out);
  not not_30 (not_30_out, D);
  and and_25 (and_25_out, A, not_31_out);
  not not_31 (not_31_out, B);
  and and_26 (and_26_out, C, not_32_out);
  not not_32 (not_32_out, D);
  and and_27 (and_27_out, A, not_33_out);
  not not_33 (not_33_out, B);
  and and_28 (and_28_out, C, D);
  not not_34 (not_34_out, C);
  not not_35 (not_35_out, A);
  and and_29 (and_29_out, not_35_out, not_36_out);
  not not_36 (not_36_out, B);
  not not_37 (not_37_out, C);
  and and_30 (and_30_out, not_37_out, not_38_out);
  not not_38 (not_38_out, D);
  not not_39 (not_39_out, A);
  and and_31 (and_31_out, not_39_out, not_40_out);
  not not_40 (not_40_out, B);
  not not_41 (not_41_out, C);
  and and_32 (and_32_out, not_41_out, D);
  not not_42 (not_42_out, A);
  not not_43 (not_43_out, C);
  not not_44 (not_44_out, A);
  not not_45 (not_45_out, D);
  not not_46 (not_46_out, B);
  not not_47 (not_47_out, C);
  not not_48 (not_48_out, D);
  not not_49 (not_49_out, B);
  not not_50 (not_50_out, D);
  not not_51 (not_51_out, C);
  not not_52 (not_52_out, D);
  not not_53 (not_53_out, C);
  not not_54 (not_54_out, A);
  not not_55 (not_55_out, D);
  not not_56 (not_56_out, A);
  and and_33 (and_33_out, not_56_out, not_57_out);
  not not_57 (not_57_out, B);
  not not_58 (not_58_out, C);
  and and_34 (and_34_out, not_58_out, D);
  not not_59 (not_59_out, A);
  and and_35 (and_35_out, not_59_out, not_60_out);
  not not_60 (not_60_out, B);
  and and_36 (and_36_out, C, not_61_out);
  not not_61 (not_61_out, D);
  not not_62 (not_62_out, A);
  not not_63 (not_63_out, B);
  not not_64 (not_64_out, A);
  not not_65 (not_65_out, C);
  not not_66 (not_66_out, B);
  not not_67 (not_67_out, C);
  not not_68 (not_68_out, D);
  not not_69 (not_69_out, B);
  not not_70 (not_70_out, C);
  not not_71 (not_71_out, B);
  not not_72 (not_72_out, D);
  not not_73 (not_73_out, C);
  not not_74 (not_74_out, D);
  not not_75 (not_75_out, C);
  not not_76 (not_76_out, A);
  and and_37 (and_37_out, not_76_out, not_77_out);
  not not_77 (not_77_out, B);
  not not_78 (not_78_out, C);
  and and_38 (and_38_out, not_78_out, not_79_out);
  not not_79 (not_79_out, D);
  not not_80 (not_80_out, A);
  and and_39 (and_39_out, not_80_out, not_81_out);
  not not_81 (not_81_out, B);
  not not_82 (not_82_out, C);
  and and_40 (and_40_out, not_82_out, D);
  not not_83 (not_83_out, A);
  not not_84 (not_84_out, D);
  and and_41 (and_41_out, A, not_85_out);
  not not_85 (not_85_out, B);
  not not_86 (not_86_out, C);
  and and_42 (and_42_out, not_86_out, not_87_out);
  not not_87 (not_87_out, D);
  and and_43 (and_43_out, A, not_88_out);
  not not_88 (not_88_out, B);
  and and_44 (and_44_out, C, not_89_out);
  not not_89 (not_89_out, D);
  not not_90 (not_90_out, A);
  not not_91 (not_91_out, D);
  not not_92 (not_92_out, A);
  and and_45 (and_45_out, not_92_out, not_93_out);
  not not_93 (not_93_out, B);
  and and_46 (and_46_out, C, D);
  not not_94 (not_94_out, A);
  and and_47 (and_47_out, not_94_out, not_95_out);
  not not_95 (not_95_out, B);
  and and_48 (and_48_out, C, not_96_out);
  not not_96 (not_96_out, D);
  not not_97 (not_97_out, A);
  not not_98 (not_98_out, C);
  not not_99 (not_99_out, D);
  not not_100 (not_100_out, A);
  and and_49 (and_49_out, not_100_out, B);
  and and_50 (and_50_out, C, D);
  and and_51 (and_51_out, A, not_101_out);
  not not_101 (not_101_out, B);
  not not_102 (not_102_out, C);
  and and_52 (and_52_out, not_102_out, D);
  not not_103 (not_103_out, B);
  not not_104 (not_104_out, A);
  and and_53 (and_53_out, not_104_out, not_105_out);
  not not_105 (not_105_out, B);
  not not_106 (not_106_out, C);
  and and_54 (and_54_out, not_106_out, not_107_out);
  not not_107 (not_107_out, D);
  not not_108 (not_108_out, A);
  and and_55 (and_55_out, not_108_out, not_109_out);
  not not_109 (not_109_out, B);
  not not_110 (not_110_out, C);
  and and_56 (and_56_out, not_110_out, D);
  not not_111 (not_111_out, A);
  and and_57 (and_57_out, not_111_out, not_112_out);
  not not_112 (not_112_out, B);
  and and_58 (and_58_out, C, not_113_out);
  not not_113 (not_113_out, D);
  not not_114 (not_114_out, A);
  and and_59 (and_59_out, not_114_out, not_115_out);
  not not_115 (not_115_out, B);
  and and_60 (and_60_out, C, D);
  not not_116 (not_116_out, A);
  and and_61 (and_61_out, not_116_out, B);
  not not_117 (not_117_out, C);
  and and_62 (and_62_out, not_117_out, not_118_out);
  not not_118 (not_118_out, D);
  not not_119 (not_119_out, A);
  and and_63 (and_63_out, not_119_out, B);
  not not_120 (not_120_out, C);
  and and_64 (and_64_out, not_120_out, D);
  not not_121 (not_121_out, A);
  not not_122 (not_122_out, D);
  not not_123 (not_123_out, A);
  and and_65 (and_65_out, not_123_out, B);
  and and_66 (and_66_out, C, D);
  and and_67 (and_67_out, A, not_124_out);
  not not_124 (not_124_out, B);
  not not_125 (not_125_out, C);
  and and_68 (and_68_out, not_125_out, D);
  not not_126 (not_126_out, B);
  not not_127 (not_127_out, D);
  and and_69 (and_69_out, A, not_128_out);
  not not_128 (not_128_out, B);
  and and_70 (and_70_out, C, D);
  and and_71 (and_71_out, A, B);
  not not_129 (not_129_out, C);
  and and_72 (and_72_out, not_129_out, not_130_out);
  not not_130 (not_130_out, D);
  not not_131 (not_131_out, C);
  not not_132 (not_132_out, A);
  and and_73 (and_73_out, not_132_out, not_133_out);
  not not_133 (not_133_out, B);
  not not_134 (not_134_out, C);
  and and_74 (and_74_out, not_134_out, not_135_out);
  not not_135 (not_135_out, D);
  not not_136 (not_136_out, A);
  and and_75 (and_75_out, not_136_out, not_137_out);
  not not_137 (not_137_out, B);
  not not_138 (not_138_out, C);
  and and_76 (and_76_out, not_138_out, D);
  not not_139 (not_139_out, A);
  not not_140 (not_140_out, B);
  not not_141 (not_141_out, A);
  not not_142 (not_142_out, C);
  not not_143 (not_143_out, D);
  not not_144 (not_144_out, A);
  not not_145 (not_145_out, C);
  not not_146 (not_146_out, A);
  not not_147 (not_147_out, D);
  not not_148 (not_148_out, B);
  not not_149 (not_149_out, C);
  not not_150 (not_150_out, D);
  not not_151 (not_151_out, C);
  and and_77 (and_77_out, and_1_out, and_2_out);
  and and_78 (and_78_out, and_3_out, and_4_out);
  and and_79 (and_79_out, and_5_out, and_6_out);
  and and_80 (and_80_out, and_7_out, and_8_out);
  and and_81 (and_81_out, and_9_out, and_10_out);
  and and_82 (and_82_out, and_11_out, and_12_out);
  and and_83 (and_83_out, and_13_out, and_14_out);
  and and_84 (and_84_out, and_15_out, and_16_out);
  and and_85 (and_85_out, and_17_out, and_18_out);
  and and_86 (and_86_out, and_19_out, and_20_out);
  and and_87 (and_87_out, and_21_out, and_22_out);
  and and_88 (and_88_out, and_23_out, and_24_out);
  and and_89 (and_89_out, and_25_out, and_26_out);
  and and_90 (and_90_out, and_27_out, and_28_out);
  and and_91 (and_91_out, A, B);
  and and_92 (and_92_out, not_34_out, D);
  and and_93 (and_93_out, and_29_out, and_30_out);
  and and_94 (and_94_out, and_31_out, and_32_out);
  and and_95 (and_95_out, not_42_out, B);
  and and_96 (and_96_out, not_43_out, D);
  and and_97 (and_97_out, not_44_out, B);
  and and_98 (and_98_out, C, not_45_out);
  and and_99 (and_99_out, A, not_46_out);
  and and_100 (and_100_out, not_47_out, not_48_out);
  and and_101 (and_101_out, A, not_49_out);
  and and_102 (and_102_out, C, not_50_out);
  and and_103 (and_103_out, A, B);
  and and_104 (and_104_out, not_51_out, not_52_out);
  and and_105 (and_105_out, A, B);
  and and_106 (and_106_out, not_53_out, D);
  and and_107 (and_107_out, not_54_out, B);
  and and_108 (and_108_out, C, not_55_out);
  and and_109 (and_109_out, and_33_out, and_34_out);
  and and_110 (and_110_out, and_35_out, and_36_out);
  and and_111 (and_111_out, not_62_out, not_63_out);
  and and_112 (and_112_out, C, D);
  and and_113 (and_113_out, not_64_out, B);
  and and_114 (and_114_out, not_65_out, D);
  and and_115 (and_115_out, A, not_66_out);
  and and_116 (and_116_out, not_67_out, not_68_out);
  and and_117 (and_117_out, A, not_69_out);
  and and_118 (and_118_out, not_70_out, D);
  and and_119 (and_119_out, A, not_71_out);
  and and_120 (and_120_out, C, not_72_out);
  and and_121 (and_121_out, A, B);
  and and_122 (and_122_out, not_73_out, not_74_out);
  and and_123 (and_123_out, A, B);
  and and_124 (and_124_out, not_75_out, D);
  and and_125 (and_125_out, and_37_out, and_38_out);
  and and_126 (and_126_out, and_39_out, and_40_out);
  and and_127 (and_127_out, not_83_out, B);
  and and_128 (and_128_out, C, not_84_out);
  and and_129 (and_129_out, and_41_out, and_42_out);
  and and_130 (and_130_out, and_43_out, and_44_out);
  and and_131 (and_131_out, not_90_out, B);
  and and_132 (and_132_out, C, not_91_out);
  and and_133 (and_133_out, and_45_out, and_46_out);
  and and_134 (and_134_out, and_47_out, and_48_out);
  and and_135 (and_135_out, not_97_out, B);
  and and_136 (and_136_out, not_98_out, not_99_out);
  and and_137 (and_137_out, and_49_out, and_50_out);
  and and_138 (and_138_out, and_51_out, and_52_out);
  and and_139 (and_139_out, A, not_103_out);
  and and_140 (and_140_out, C, D);
  and and_141 (and_141_out, and_53_out, and_54_out);
  and and_142 (and_142_out, and_55_out, and_56_out);
  and and_143 (and_143_out, and_57_out, and_58_out);
  and and_144 (and_144_out, and_59_out, and_60_out);
  and and_145 (and_145_out, and_61_out, and_62_out);
  and and_146 (and_146_out, and_63_out, and_64_out);
  and and_147 (and_147_out, not_121_out, B);
  and and_148 (and_148_out, C, not_122_out);
  and and_149 (and_149_out, and_65_out, and_66_out);
  and and_150 (and_150_out, and_67_out, and_68_out);
  and and_151 (and_151_out, A, not_126_out);
  and and_152 (and_152_out, C, not_127_out);
  and and_153 (and_153_out, and_69_out, and_70_out);
  and and_154 (and_154_out, and_71_out, and_72_out);
  and and_155 (and_155_out, A, B);
  and and_156 (and_156_out, not_131_out, D);
  and and_157 (and_157_out, and_73_out, and_74_out);
  and and_158 (and_158_out, and_75_out, and_76_out);
  and and_159 (and_159_out, not_139_out, not_140_out);
  and and_160 (and_160_out, C, D);
  and and_161 (and_161_out, not_141_out, B);
  and and_162 (and_162_out, not_142_out, not_143_out);
  and and_163 (and_163_out, not_144_out, B);
  and and_164 (and_164_out, not_145_out, D);
  and and_165 (and_165_out, not_146_out, B);
  and and_166 (and_166_out, C, not_147_out);
  and and_167 (and_167_out, A, not_148_out);
  and and_168 (and_168_out, C, D);
  and and_169 (and_169_out, A, B);
  and and_170 (and_170_out, not_149_out, not_150_out);
  and and_171 (and_171_out, A, B);
  and and_172 (and_172_out, not_151_out, D);
  or or_1 (or_1_out, and_77_out, and_78_out);
  or or_2 (or_2_out, and_79_out, and_80_out);
  or or_3 (or_3_out, and_81_out, and_82_out);
  or or_4 (or_4_out, and_83_out, and_84_out);
  or or_5 (or_5_out, and_85_out, and_86_out);
  or or_6 (or_6_out, and_87_out, and_88_out);
  or or_7 (or_7_out, and_89_out, and_90_out);
  and and_173 (and_173_out, and_91_out, and_92_out);
  or or_8 (or_8_out, and_93_out, and_94_out);
  and and_174 (and_174_out, and_95_out, and_96_out);
  and and_175 (and_175_out, and_97_out, and_98_out);
  and and_176 (and_176_out, and_99_out, and_100_out);
  and and_177 (and_177_out, and_101_out, and_102_out);
  and and_178 (and_178_out, and_103_out, and_104_out);
  and and_179 (and_179_out, and_105_out, and_106_out);
  and and_180 (and_180_out, and_107_out, and_108_out);
  or or_9 (or_9_out, and_109_out, and_110_out);
  and and_181 (and_181_out, and_111_out, and_112_out);
  and and_182 (and_182_out, and_113_out, and_114_out);
  and and_183 (and_183_out, and_115_out, and_116_out);
  and and_184 (and_184_out, and_117_out, and_118_out);
  and and_185 (and_185_out, and_119_out, and_120_out);
  and and_186 (and_186_out, and_121_out, and_122_out);
  and and_187 (and_187_out, and_123_out, and_124_out);
  or or_10 (or_10_out, and_125_out, and_126_out);
  and and_188 (and_188_out, and_127_out, and_128_out);
  or or_11 (or_11_out, and_129_out, and_130_out);
  and and_189 (and_189_out, and_131_out, and_132_out);
  or or_12 (or_12_out, and_133_out, and_134_out);
  and and_190 (and_190_out, and_135_out, and_136_out);
  or or_13 (or_13_out, and_137_out, and_138_out);
  and and_191 (and_191_out, and_139_out, and_140_out);
  or or_14 (or_14_out, and_141_out, and_142_out);
  or or_15 (or_15_out, and_143_out, and_144_out);
  or or_16 (or_16_out, and_145_out, and_146_out);
  and and_192 (and_192_out, and_147_out, and_148_out);
  or or_17 (or_17_out, and_149_out, and_150_out);
  and and_193 (and_193_out, and_151_out, and_152_out);
  or or_18 (or_18_out, and_153_out, and_154_out);
  and and_194 (and_194_out, and_155_out, and_156_out);
  or or_19 (or_19_out, and_157_out, and_158_out);
  and and_195 (and_195_out, and_159_out, and_160_out);
  and and_196 (and_196_out, and_161_out, and_162_out);
  and and_197 (and_197_out, and_163_out, and_164_out);
  and and_198 (and_198_out, and_165_out, and_166_out);
  and and_199 (and_199_out, and_167_out, and_168_out);
  and and_200 (and_200_out, and_169_out, and_170_out);
  and and_201 (and_201_out, and_171_out, and_172_out);
  or or_20 (or_20_out, or_1_out, or_2_out);
  or or_21 (or_21_out, or_3_out, or_4_out);
  or or_22 (or_22_out, or_5_out, or_6_out);
  or or_23 (or_23_out, or_7_out, and_173_out);
  or or_24 (or_24_out, or_8_out, and_174_out);
  or or_25 (or_25_out, and_175_out, and_176_out);
  or or_26 (or_26_out, and_177_out, and_178_out);
  or or_27 (or_27_out, and_179_out, and_180_out);
  or or_28 (or_28_out, or_9_out, and_181_out);
  or or_29 (or_29_out, and_182_out, and_183_out);
  or or_30 (or_30_out, and_184_out, and_185_out);
  or or_31 (or_31_out, and_186_out, and_187_out);
  or or_32 (or_32_out, or_10_out, and_188_out);
  or or_33 (or_33_out, or_11_out, and_189_out);
  or or_34 (or_34_out, or_12_out, and_190_out);
  or or_35 (or_35_out, or_13_out, and_191_out);
  or or_36 (or_36_out, or_14_out, or_15_out);
  or or_37 (or_37_out, or_16_out, and_192_out);
  or or_38 (or_38_out, or_17_out, and_193_out);
  or or_39 (or_39_out, or_18_out, and_194_out);
  or or_40 (or_40_out, or_19_out, and_195_out);
  or or_41 (or_41_out, and_196_out, and_197_out);
  or or_42 (or_42_out, and_198_out, and_199_out);
  or or_43 (or_43_out, and_200_out, and_201_out);
  or or_44 (a_2, or_20_out, or_21_out);
  or or_45 (b_2, or_22_out, or_23_out);
  or or_46 (or_46_out, or_24_out, or_25_out);
  or or_47 (or_47_out, or_26_out, or_27_out);
  or or_48 (or_48_out, or_28_out, or_29_out);
  or or_49 (or_49_out, or_30_out, or_31_out);
  or or_50 (or_50_out, or_32_out, or_33_out);
  or or_51 (or_51_out, or_34_out, or_35_out);
  or or_52 (or_52_out, or_36_out, or_37_out);
  or or_53 (or_53_out, or_38_out, or_39_out);
  or or_54 (or_54_out, or_40_out, or_41_out);
  or or_55 (or_55_out, or_42_out, or_43_out);
  or or_56 (c_2, or_46_out, or_47_out);
  or or_57 (d_2, or_48_out, or_49_out);
  or or_58 (e, or_50_out, or_51_out);
  or or_59 (f, or_52_out, or_53_out);
  or or_60 (g, or_54_out, or_55_out);

  assign P = 1'b0;
endmodule

module COMPLETO (
  input  A,
  input  B,
  input  C,
  input  D,
  output a_2,
  output b_2,
  output c_2,
  output d_2,
  output e,
  output f,
  output g,
  output P
);

  wire and_1_out, and_2_out, and_3_out, and_4_out, and_5_out, and_6_out, and_7_out, and_8_out, and_9_out,
       and_10_out, and_11_out, and_12_out, and_13_out, and_14_out, and_15_out, and_16_out, and_17_out,
       and_18_out, and_19_out, and_20_out, and_21_out, and_22_out, and_23_out, and_24_out, and_25_out,
       and_26_out, and_27_out, and_28_out, and_29_out, and_30_out, and_31_out, and_32_out, and_33_out,
       and_34_out, and_35_out, and_36_out, and_37_out, and_38_out, and_39_out, and_40_out, and_41_out,
       and_42_out, and_43_out, and_44_out, and_45_out, and_46_out, and_47_out, and_48_out, and_49_out,
       and_50_out, and_51_out, and_52_out, and_53_out, and_54_out, and_55_out, and_56_out, and_57_out,
       and_58_out, and_59_out, and_60_out, and_61_out, and_62_out, and_63_out, and_64_out, and_65_out,
       and_66_out, not_1_out, not_2_out, not_3_out, not_4_out, not_5_out, not_6_out, not_7_out, not_8_out,
       not_9_out, not_10_out, not_11_out, not_12_out, not_13_out, not_14_out, not_15_out, not_16_out,
       not_17_out, not_18_out, not_19_out, not_20_out, not_21_out, not_22_out, not_23_out, not_24_out,
       not_25_out, not_26_out, not_27_out, not_28_out, not_29_out, not_30_out, not_31_out, not_32_out,
       not_33_out, not_34_out, not_35_out, not_36_out, not_37_out, not_38_out, not_39_out, not_40_out,
       not_41_out, not_42_out, not_43_out, not_44_out, not_45_out, not_46_out, not_47_out, not_48_out,
       not_49_out, not_50_out, not_51_out, not_52_out, not_53_out, not_54_out, not_55_out, not_56_out,
       not_57_out, not_58_out, not_59_out, not_60_out, not_61_out, not_62_out, not_63_out, not_64_out,
       not_65_out, not_66_out, not_67_out, not_68_out, not_69_out, not_70_out, not_71_out, not_72_out,
       not_73_out, not_74_out, not_75_out, not_76_out, not_77_out, not_78_out, not_79_out, not_80_out,
       not_81_out, not_82_out, not_83_out, not_84_out, not_85_out, not_86_out, not_87_out, not_88_out,
       not_89_out, not_90_out, not_91_out, not_92_out, not_93_out, not_94_out, not_95_out, not_96_out,
       not_97_out, not_98_out, not_99_out, not_100_out, not_101_out, not_102_out, not_103_out, not_104_out,
       not_105_out, not_106_out, not_107_out, not_108_out, not_109_out, not_110_out, not_111_out,
       not_112_out, not_113_out, not_114_out, not_115_out, not_116_out, not_117_out, not_118_out,
       not_119_out, not_120_out, not_121_out, not_122_out, not_123_out, not_124_out, not_125_out,
       not_126_out, not_127_out, not_128_out, not_129_out, not_130_out, not_131_out, not_132_out,
       not_133_out, not_134_out, not_135_out, not_136_out, not_137_out, not_138_out, not_139_out,
       not_140_out, not_141_out, not_142_out, not_143_out, not_144_out, not_145_out, not_146_out,
       not_147_out, not_148_out, not_149_out, not_150_out;

  not not_1 (not_1_out, A);
  not not_2 (not_2_out, B);
  not not_3 (not_3_out, C);
  not not_4 (not_4_out, D);
  not not_5 (not_5_out, A);
  not not_6 (not_6_out, B);
  not not_7 (not_7_out, D);
  not not_8 (not_8_out, A);
  not not_9 (not_9_out, B);
  not not_10 (not_10_out, A);
  not not_11 (not_11_out, C);
  not not_12 (not_12_out, D);
  not not_13 (not_13_out, A);
  not not_14 (not_14_out, C);
  not not_15 (not_15_out, B);
  not not_16 (not_16_out, D);
  not not_17 (not_17_out, B);
  not not_18 (not_18_out, C);
  not not_19 (not_19_out, D);
  not not_20 (not_20_out, A);
  not not_21 (not_21_out, B);
  not not_22 (not_22_out, C);
  not not_23 (not_23_out, D);
  not not_24 (not_24_out, A);
  not not_25 (not_25_out, C);
  not not_26 (not_26_out, A);
  not not_27 (not_27_out, D);
  not not_28 (not_28_out, B);
  not not_29 (not_29_out, C);
  not not_30 (not_30_out, D);
  not not_31 (not_31_out, B);
  not not_32 (not_32_out, D);
  not not_33 (not_33_out, B);
  not not_34 (not_34_out, C);
  not not_35 (not_35_out, A);
  not not_36 (not_36_out, B);
  not not_37 (not_37_out, C);
  not not_38 (not_38_out, D);
  not not_39 (not_39_out, A);
  not not_40 (not_40_out, B);
  not not_41 (not_41_out, C);
  not not_42 (not_42_out, A);
  not not_43 (not_43_out, C);
  not not_44 (not_44_out, A);
  not not_45 (not_45_out, D);
  not not_46 (not_46_out, B);
  not not_47 (not_47_out, C);
  not not_48 (not_48_out, D);
  not not_49 (not_49_out, B);
  not not_50 (not_50_out, D);
  not not_51 (not_51_out, C);
  not not_52 (not_52_out, C);
  not not_53 (not_53_out, D);
  not not_54 (not_54_out, A);
  not not_55 (not_55_out, B);
  not not_56 (not_56_out, C);
  not not_57 (not_57_out, A);
  not not_58 (not_58_out, B);
  not not_59 (not_59_out, D);
  not not_60 (not_60_out, A);
  not not_61 (not_61_out, B);
  not not_62 (not_62_out, A);
  not not_63 (not_63_out, C);
  not not_64 (not_64_out, B);
  not not_65 (not_65_out, C);
  not not_66 (not_66_out, D);
  not not_67 (not_67_out, B);
  not not_68 (not_68_out, C);
  not not_69 (not_69_out, B);
  not not_70 (not_70_out, D);
  not not_71 (not_71_out, C);
  not not_72 (not_72_out, D);
  not not_73 (not_73_out, C);
  not not_74 (not_74_out, A);
  not not_75 (not_75_out, B);
  not not_76 (not_76_out, C);
  not not_77 (not_77_out, D);
  not not_78 (not_78_out, A);
  not not_79 (not_79_out, B);
  not not_80 (not_80_out, C);
  not not_81 (not_81_out, A);
  not not_82 (not_82_out, B);
  not not_83 (not_83_out, D);
  not not_84 (not_84_out, A);
  not not_85 (not_85_out, B);
  not not_86 (not_86_out, A);
  not not_87 (not_87_out, C);
  not not_88 (not_88_out, D);
  not not_89 (not_89_out, A);
  not not_90 (not_90_out, B);
  not not_91 (not_91_out, C);
  not not_92 (not_92_out, D);
  not not_93 (not_93_out, B);
  not not_94 (not_94_out, C);
  not not_95 (not_95_out, D);
  not not_96 (not_96_out, B);
  not not_97 (not_97_out, C);
  not not_98 (not_98_out, B);
  not not_99 (not_99_out, D);
  not not_100 (not_100_out, B);
  not not_101 (not_101_out, A);
  not not_102 (not_102_out, D);
  not not_103 (not_103_out, A);
  not not_104 (not_104_out, B);
  not not_105 (not_105_out, C);
  not not_106 (not_106_out, D);
  not not_107 (not_107_out, A);
  not not_108 (not_108_out, B);
  not not_109 (not_109_out, C);
  not not_110 (not_110_out, A);
  not not_111 (not_111_out, B);
  not not_112 (not_112_out, D);
  not not_113 (not_113_out, A);
  not not_114 (not_114_out, B);
  not not_115 (not_115_out, A);
  not not_116 (not_116_out, C);
  not not_117 (not_117_out, D);
  not not_118 (not_118_out, A);
  not not_119 (not_119_out, C);
  not not_120 (not_120_out, A);
  not not_121 (not_121_out, D);
  not not_122 (not_122_out, A);
  not not_123 (not_123_out, B);
  not not_124 (not_124_out, C);
  not not_125 (not_125_out, B);
  not not_126 (not_126_out, D);
  not not_127 (not_127_out, B);
  not not_128 (not_128_out, C);
  not not_129 (not_129_out, D);
  not not_130 (not_130_out, C);
  not not_131 (not_131_out, A);
  not not_132 (not_132_out, B);
  not not_133 (not_133_out, C);
  not not_134 (not_134_out, D);
  not not_135 (not_135_out, A);
  not not_136 (not_136_out, B);
  not not_137 (not_137_out, C);
  not not_138 (not_138_out, A);
  not not_139 (not_139_out, B);
  not not_140 (not_140_out, A);
  not not_141 (not_141_out, C);
  not not_142 (not_142_out, D);
  not not_143 (not_143_out, A);
  not not_144 (not_144_out, C);
  not not_145 (not_145_out, A);
  not not_146 (not_146_out, D);
  not not_147 (not_147_out, B);
  not not_148 (not_148_out, C);
  not not_149 (not_149_out, D);
  not not_150 (not_150_out, C);
  and and_1 (and_1_out, not_1_out, not_2_out, not_3_out, not_4_out);
  and and_2 (and_2_out, not_5_out, not_6_out, C, not_7_out);
  and and_3 (and_3_out, not_8_out, not_9_out, C, D);
  and and_4 (and_4_out, not_10_out, B, not_11_out, not_12_out);
  and and_5 (and_5_out, not_13_out, B, not_14_out, D);
  and and_6 (and_6_out, A, not_15_out, C, not_16_out);
  and and_7 (and_7_out, A, not_17_out, C, D);
  and and_8 (and_8_out, A, B, not_18_out, not_19_out);
  and and_9 (and_9_out, not_20_out, not_21_out, not_22_out, not_23_out);
  and and_10 (and_10_out, not_24_out, B, not_25_out, D);
  and and_11 (and_11_out, not_26_out, B, C, not_27_out);
  and and_12 (and_12_out, A, not_28_out, not_29_out, not_30_out);
  and and_13 (and_13_out, A, not_31_out, C, not_32_out);
  and and_14 (and_14_out, A, not_33_out, C, D);
  and and_15 (and_15_out, A, B, not_34_out, D);
  and and_16 (and_16_out, not_35_out, not_36_out, not_37_out, not_38_out);
  and and_17 (and_17_out, not_39_out, not_40_out, not_41_out, D);
  and and_18 (and_18_out, not_42_out, B, not_43_out, D);
  and and_19 (and_19_out, not_44_out, B, C, not_45_out);
  and and_20 (and_20_out, A, not_46_out, not_47_out, not_48_out);
  and and_21 (and_21_out, A, not_49_out, C, not_50_out);
  and and_22 (and_22_out, A, B, not_51_out, D);
  and and_23 (and_23_out, A, B, not_52_out, not_53_out);
  and and_24 (and_24_out, not_54_out, not_55_out, not_56_out, D);
  and and_25 (and_25_out, not_57_out, not_58_out, C, not_59_out);
  and and_26 (and_26_out, not_60_out, not_61_out, C, D);
  and and_27 (and_27_out, not_62_out, B, not_63_out, D);
  and and_28 (and_28_out, A, not_64_out, not_65_out, not_66_out);
  and and_29 (and_29_out, A, not_67_out, not_68_out, D);
  and and_30 (and_30_out, A, not_69_out, C, not_70_out);
  and and_31 (and_31_out, A, B, not_71_out, not_72_out);
  and and_32 (and_32_out, A, B, not_73_out, D);
  and and_33 (and_33_out, not_74_out, not_75_out, not_76_out, not_77_out);
  and and_34 (and_34_out, not_78_out, not_79_out, not_80_out, D);
  and and_35 (and_35_out, not_81_out, not_82_out, C, not_83_out);
  and and_36 (and_36_out, not_84_out, not_85_out, C, D);
  and and_37 (and_37_out, not_86_out, B, not_87_out, not_88_out);
  and and_38 (and_38_out, not_89_out, B, C, D);
  and and_39 (and_39_out, A, not_90_out, not_91_out, not_92_out);
  and and_40 (and_40_out, A, not_93_out, not_94_out, not_95_out);
  and and_41 (and_41_out, A, not_96_out, not_97_out, D);
  and and_42 (and_42_out, A, not_98_out, C, not_99_out);
  and and_43 (and_43_out, A, not_100_out, C, D);
  and and_44 (and_44_out, not_101_out, B, C, not_102_out);
  and and_45 (and_45_out, not_103_out, not_104_out, not_105_out, not_106_out);
  and and_46 (and_46_out, not_107_out, not_108_out, not_109_out, D);
  and and_47 (and_47_out, not_110_out, not_111_out, C, not_112_out);
  and and_48 (and_48_out, not_113_out, not_114_out, C, D);
  and and_49 (and_49_out, not_115_out, B, not_116_out, not_117_out);
  and and_50 (and_50_out, not_118_out, B, not_119_out, D);
  and and_51 (and_51_out, not_120_out, B, C, not_121_out);
  and and_52 (and_52_out, not_122_out, B, C, D);
  and and_53 (and_53_out, A, not_123_out, not_124_out, D);
  and and_54 (and_54_out, A, not_125_out, C, not_126_out);
  and and_55 (and_55_out, A, not_127_out, C, D);
  and and_56 (and_56_out, A, B, not_128_out, not_129_out);
  and and_57 (and_57_out, A, B, not_130_out, D);
  and and_58 (and_58_out, not_131_out, not_132_out, not_133_out, not_134_out);
  and and_59 (and_59_out, not_135_out, not_136_out, not_137_out, D);
  and and_60 (and_60_out, not_138_out, not_139_out, C, D);
  and and_61 (and_61_out, not_140_out, B, not_141_out, not_142_out);
  and and_62 (and_62_out, not_143_out, B, not_144_out, D);
  and and_63 (and_63_out, not_145_out, B, C, not_146_out);
  and and_64 (and_64_out, A, not_147_out, C, D);
  and and_65 (and_65_out, A, B, not_148_out, not_149_out);
  and and_66 (and_66_out, A, B, not_150_out, D);
  or or_1 (a_2, and_1_out, and_2_out, and_3_out, and_4_out, and_5_out, and_6_out, and_7_out, and_8_out);
  or or_2 (b_2, and_9_out, and_10_out, and_11_out, and_12_out, and_13_out, and_14_out, and_15_out);
  or or_3 (c_2, and_16_out, and_17_out, and_18_out, and_19_out, and_20_out, and_21_out, and_22_out, and_23_out);
  or or_4 (d_2, and_24_out, and_25_out, and_26_out, and_27_out, and_28_out, and_29_out, and_30_out, and_31_out, and_32_out);
  or or_5 (e, and_33_out, and_34_out, and_35_out, and_36_out, and_37_out, and_38_out, and_39_out, and_40_out, and_41_out, and_42_out, and_43_out, and_44_out);
  or or_6 (f, and_45_out, and_46_out, and_47_out, and_48_out, and_49_out, and_50_out, and_51_out, and_52_out, and_53_out, and_54_out, and_55_out, and_56_out, and_57_out);
  or or_7 (g, and_58_out, and_59_out, and_60_out, and_61_out, and_62_out, and_63_out, and_64_out, and_65_out, and_66_out);

  assign P = 1'b0;
endmodule
