// Logisim project letras completo.circ as structural Verilog
module Letras (
  input  A,
  input  B,
  input  C,
  input  D,
  output e,
  output c_2,
  output a_2,
  output f,
  output g,
  output d_2,
  output b_2,
  output P
);

  wire and_1_out, and_2_out, and_3_out, and_4_out, and_5_out, and_6_out, and_7_out, and_8_out, and_9_out,
       and_10_out, and_11_out, and_12_out, and_13_out, and_14_out, and_15_out, and_16_out, and_17_out,
       and_18_out, and_19_out, and_20_out, not_1_out, not_2_out, not_3_out, not_4_out, not_5_out, not_6_out,
       not_7_out, not_8_out, not_9_out, not_10_out, not_11_out, not_12_out, not_13_out, not_14_out,
       not_15_out, not_16_out, not_17_out, not_18_out, not_19_out, not_20_out, not_21_out, not_22_out,
       not_23_out, not_24_out, not_25_out, not_26_out, not_27_out, not_28_out, not_29_out, not_30_out,
       not_31_out, not_32_out;

  not not_1 (not_1_out, A);
  not not_2 (not_2_out, B);
  and and_1 (and_1_out, not_1_out, not_2_out, not_3_out);
  not not_3 (not_3_out, D);
  not not_4 (not_4_out, B);
  and and_2 (and_2_out, not_4_out, C);
  not not_5 (not_5_out, A);
  and and_3 (and_3_out, not_5_out, B, not_6_out);
  not not_6 (not_6_out, C);
  not not_7 (not_7_out, C);
  and and_4 (and_4_out, B, not_7_out, not_8_out);
  not not_8 (not_8_out, D);
  not not_9 (not_9_out, B);
  and and_5 (and_5_out, not_9_out, not_10_out, not_11_out);
  not not_10 (not_10_out, C);
  not not_11 (not_11_out, D);
  not not_12 (not_12_out, C);
  and and_6 (and_6_out, B, not_12_out, D);
  and and_7 (and_7_out, B, C, not_13_out);
  not not_13 (not_13_out, D);
  and and_8 (and_8_out, A, C);
  or or_1 (a_2, and_1_out, and_2_out, and_3_out, and_4_out);
  or or_2 (b_2, and_5_out, and_6_out, and_7_out, and_8_out);
  not not_14 (not_14_out, A);
  not not_15 (not_15_out, B);
  not not_16 (not_16_out, C);
  not not_17 (not_17_out, C);
  not not_18 (not_18_out, D);
  not not_19 (not_19_out, D);
  not not_20 (not_20_out, C);
  not not_21 (not_21_out, A);
  not not_22 (not_22_out, B);
  not not_23 (not_23_out, D);
  and and_9 (and_9_out, not_14_out, not_15_out, not_16_out);
  and and_10 (and_10_out, B, not_17_out, D);
  and and_11 (and_11_out, B, C, not_18_out);
  and and_12 (and_12_out, A, not_19_out);
  and and_13 (and_13_out, not_20_out, D);
  and and_14 (and_14_out, not_21_out, not_22_out, C);
  and and_15 (and_15_out, A, not_23_out);
  or or_3 (c_2, and_9_out, and_10_out, and_11_out, and_12_out);
  or or_4 (d_2, and_13_out, and_14_out, and_15_out);
  not not_24 (not_24_out, A);
  not not_25 (not_25_out, D);
  not not_26 (not_26_out, A);
  not not_27 (not_27_out, A);
  not not_28 (not_28_out, C);
  not not_29 (not_29_out, B);
  not not_30 (not_30_out, C);
  not not_31 (not_31_out, D);
  and and_16 (and_16_out, not_24_out, not_25_out);
  not not_32 (not_32_out, B);
  or or_5 (f, not_26_out, D, C, B);
  and and_17 (and_17_out, not_27_out, not_28_out);
  and and_18 (and_18_out, not_29_out, C, D);
  and and_19 (and_19_out, B, not_30_out);
  and and_20 (and_20_out, B, not_31_out);
  or or_6 (e, and_16_out, not_32_out, C);
  or or_7 (g, and_17_out, and_18_out, and_19_out, and_20_out);

  assign P = 1'b0;
endmodule
