// Logisim project 4x1.circ as structural Verilog: 1 circuit, main circuit main
module main (
  input  A,
  input  [1:0] C
);

  wire multiplexer_1_out, not_1_out;

  not not_1 (not_1_out, A);
  Multiplexer #(.select(2)) multiplexer_1 (
    .in0(1'b1), .in1(not_1_out), .in2(not_1_out), .in3(1'b0), .out(multiplexer_1_out), .sel(C));  // open: en
  LED led_1 (.in(multiplexer_1_out));

  // Notes on the sheet:
  //   1
  //   0
  //   B
endmodule
