// Logisim project 8x1.circ as structural Verilog: 1 circuit, main circuit main
module main (
  input  I0,
  input  I1,
  input  I2,
  input  I3,
  input  I4,
  input  I5,
  input  I6,
  input  [2:0] Ps2,
  input  I7
);

  wire multiplexer_1_out;

  Multiplexer #(.select(3)) multiplexer_1 (
    .in0(I0), .in1(I1), .in2(I2), .in3(I3), .in4(I4), .in5(I5), .in6(I6), .in7(I7), .out(multiplexer_1_out),
    .sel(Ps2));  // open: en
  LED led_1 (.in(multiplexer_1_out));

  // Notes on the sheet:
  //   Ps1
  //   Ps3
endmodule
