// Logisim project 8x1.circ as structural Verilog: 1 circuit, main circuit main
module main (
  input  i0,
  input  i1,
  input  i2,
  input  i3,
  input  i4,
  input  i5,
  input  i6,
  input  [2:0] Ps2,
  input  i7
);

  wire multiplexer_1_out;

  Multiplexer #(.select(3)) multiplexer_1 (
    .in0(i0), .in1(i1), .in2(i2), .in3(i3), .in4(i4), .in5(i5), .in6(i6), .in7(i7), .out(multiplexer_1_out),
    .sel(Ps2));  // open: en
  LED led_1 (.in(multiplexer_1_out));

  // Notes on the sheet:
  //   Ps1
  //   Ps3
endmodule
